// Logisim project full_circuit.circ as structural Verilog
module main (
  input  [7:0] in_1,
  input  [7:0] in_2,
  input  [1:0] in_3
);

  wire and_1_out, BTNC_out, clock_1_out, IS_PRODUCT_NEGATIVE_out, nor_1_out, not_1_out, not_2_out,
       shiftright_1_out_5;
  wire [3:0] binary_to_bcd_1_a, binary_to_bcd_1_b, binary_to_bcd_1_c, binary_to_bcd_1_d, binary_to_bcd_1_e;
  wire [7:0] multiplexer_1_out, multiplexer_2_out, shiftleft_1_cur_val, shiftright_1_cur_val,
       twos_comp_1_out_2, twos_comp_2_out_2;
  wire [13:0] adder_1_out, multiplexer_3_out, rgstr_1_cur_value;

  Clock clock_1 (.out(clock_1_out));
  xor IS_PRODUCT_NEGATIVE (IS_PRODUCT_NEGATIVE_out, in_2[7], in_1[7]);
  twos_comp twos_comp_1 (.num_in(in_1), .out_2(twos_comp_1_out_2));
  twos_comp twos_comp_2 (.num_in(in_2), .out_2(twos_comp_2_out_2));
  Button BTNC (.out(BTNC_out));
  Multiplexer #(.width(8)) multiplexer_1 (.in0(in_1), .in1(twos_comp_1_out_2), .out(multiplexer_1_out), .sel(in_1[7]));
  Multiplexer #(.width(8)) multiplexer_2 (.in0(in_2), .in1(twos_comp_2_out_2), .out(multiplexer_2_out), .sel(in_2[7]));
  not not_1 (not_1_out, nor_1_out);
  ShiftLeft shiftleft_1 (
    .inpt(multiplexer_1_out), .Clk(clock_1_out), .EN(not_1_out), .Load(BTNC_out),
    .cur_val(shiftleft_1_cur_val));  // open: lsb
  ShiftRight shiftright_1 (
    .inpt(multiplexer_2_out), .clk(clock_1_out), .EN(not_1_out), .Load(BTNC_out), .out_5(shiftright_1_out_5),
    .cur_val(shiftright_1_cur_val));
  nor nor_1 (nor_1_out, shiftright_1_cur_val[7], shiftright_1_cur_val[6], shiftright_1_cur_val[5], shiftright_1_cur_val[4], shiftright_1_cur_val[3], shiftright_1_cur_val[2], shiftright_1_cur_val[1], shiftright_1_cur_val[0]);
  LED end_of_multiplication (.in(nor_1_out));
  Multiplexer #(.width(14)) multiplexer_3 (
    .in0({14{1'b0}}), .in1({{6{1'b0}}, shiftleft_1_cur_val}), .out(multiplexer_3_out),
    .sel(shiftright_1_out_5));
  Adder #(.width(14)) adder_1 (
    .a(multiplexer_3_out), .b(rgstr_1_cur_value), .out(adder_1_out), .cin(1'b0));  // open: cout
  and and_1 (and_1_out, not_1_out, not_2_out);
  not not_2 (not_2_out, BTNC_out);
  Rgstr rgstr_1 (
    .inpt(adder_1_out), .Clk(clock_1_out), .Reset(BTNC_out), .EP(and_1_out), .cur_value(rgstr_1_cur_value));
  binary_to_bcd binary_to_bcd_1 (
    .in_1({2'b00, rgstr_1_cur_value}), .a(binary_to_bcd_1_a), .b(binary_to_bcd_1_b), .c(binary_to_bcd_1_c),
    .d(binary_to_bcd_1_d), .e(binary_to_bcd_1_e));
  _7_Segment_Display u_7_segment_display_1 (.g(IS_PRODUCT_NEGATIVE_out));  // open: f, a, b, e, d, c, dp
  _7_Segment_Display u_7_segment_display_2 ();  // open: g, f, a, b, e, d, c, dp
  // BCD_to_7_Segment_decoder bcd_to_7_segment_decoder_1: pin names not known
  Multiplexer #(.select(2), .width(4)) multiplexer_4 (
    .in0(binary_to_bcd_1_c), .in1(binary_to_bcd_1_d), .in2(binary_to_bcd_1_e), .sel(in_3));  // open: in3, out
  _7_Segment_Display u_7_segment_display_3 ();  // open: g, f, a, b, e, d, c, dp
  // BCD_to_7_Segment_decoder bcd_to_7_segment_decoder_2: pin names not known
  Multiplexer #(.select(2), .width(4)) multiplexer_5 (
    .in0(binary_to_bcd_1_b), .in1(binary_to_bcd_1_c), .in2(binary_to_bcd_1_d), .sel(in_3));  // open: in3, out
  _7_Segment_Display u_7_segment_display_4 ();  // open: g, f, a, b, e, d, c, dp
  // BCD_to_7_Segment_decoder bcd_to_7_segment_decoder_3: pin names not known
  Multiplexer #(.select(2), .width(4)) multiplexer_6 (
    .in0(binary_to_bcd_1_a), .in1(binary_to_bcd_1_b), .in2(binary_to_bcd_1_c), .sel(in_3));  // open: in3, out
endmodule

module ShiftLeft (
  input  [7:0] inpt,
  input  Clk,
  input  EN,
  input  Load,
  output lsb,
  output [7:0] cur_val
);

  wire multiplexer_1_out, multiplexer_2_out, multiplexer_3_out, multiplexer_4_out, multiplexer_5_out,
       multiplexer_6_out, multiplexer_7_out, multiplexer_8_out, multiplexer_9_out, multiplexer_10_out,
       multiplexer_11_out, multiplexer_12_out, multiplexer_13_out, multiplexer_14_out, multiplexer_15_out,
       multiplexer_16_out;

  Multiplexer multiplexer_1 (.in0(cur_val[7]), .in1(cur_val[6]), .out(multiplexer_1_out), .sel(EN));
  D_Flip_Flop d_ff_1 (.D(multiplexer_2_out), .clk(Clk), .Q(cur_val[7]));  // open: Qn, preset, reset
  Multiplexer multiplexer_2 (.in0(multiplexer_1_out), .in1(inpt[7]), .out(multiplexer_2_out), .sel(Load));
  D_Flip_Flop d_ff_2 (.D(multiplexer_4_out), .clk(Clk), .Q(cur_val[6]));  // open: Qn, preset, reset
  Multiplexer multiplexer_3 (.in0(cur_val[6]), .in1(cur_val[5]), .out(multiplexer_3_out), .sel(EN));
  Multiplexer multiplexer_4 (.in0(multiplexer_3_out), .in1(inpt[6]), .out(multiplexer_4_out), .sel(Load));
  Multiplexer multiplexer_5 (.in0(cur_val[5]), .in1(cur_val[4]), .out(multiplexer_5_out), .sel(EN));
  D_Flip_Flop d_ff_3 (.D(multiplexer_6_out), .clk(Clk), .Q(cur_val[5]));  // open: Qn, preset, reset
  Multiplexer multiplexer_6 (.in0(multiplexer_5_out), .in1(inpt[5]), .out(multiplexer_6_out), .sel(Load));
  Multiplexer multiplexer_7 (.in0(cur_val[4]), .in1(cur_val[3]), .out(multiplexer_7_out), .sel(EN));
  D_Flip_Flop d_ff_4 (.D(multiplexer_8_out), .clk(Clk), .Q(cur_val[4]));  // open: Qn, preset, reset
  Multiplexer multiplexer_8 (.in0(multiplexer_7_out), .in1(inpt[4]), .out(multiplexer_8_out), .sel(Load));
  Multiplexer multiplexer_9 (.in0(cur_val[3]), .in1(cur_val[2]), .out(multiplexer_9_out), .sel(EN));
  D_Flip_Flop d_ff_5 (.D(multiplexer_10_out), .clk(Clk), .Q(cur_val[3]));  // open: Qn, preset, reset
  Multiplexer multiplexer_10 (.in0(multiplexer_9_out), .in1(inpt[3]), .out(multiplexer_10_out), .sel(Load));
  D_Flip_Flop d_ff_6 (.D(multiplexer_12_out), .clk(Clk), .Q(cur_val[2]));  // open: Qn, preset, reset
  Multiplexer multiplexer_11 (.in0(cur_val[2]), .in1(cur_val[1]), .out(multiplexer_11_out), .sel(EN));
  Multiplexer multiplexer_12 (.in0(multiplexer_11_out), .in1(inpt[2]), .out(multiplexer_12_out), .sel(Load));
  Multiplexer multiplexer_13 (.in0(cur_val[1]), .in1(cur_val[0]), .out(multiplexer_13_out), .sel(EN));
  D_Flip_Flop d_ff_7 (.D(multiplexer_14_out), .clk(Clk), .Q(cur_val[1]));  // open: Qn, preset, reset
  Multiplexer multiplexer_14 (.in0(multiplexer_13_out), .in1(inpt[1]), .out(multiplexer_14_out), .sel(Load));
  Multiplexer multiplexer_15 (.in0(cur_val[0]), .in1(1'b0), .out(multiplexer_15_out), .sel(EN));
  D_Flip_Flop d_ff_8 (.D(multiplexer_16_out), .clk(Clk), .Q(cur_val[0]));  // open: Qn, preset, reset
  Multiplexer multiplexer_16 (.in0(multiplexer_15_out), .in1(inpt[0]), .out(multiplexer_16_out), .sel(Load));

  assign lsb = cur_val[0];
endmodule

module ShiftRight (
  input  [7:0] inpt,
  input  clk,
  input  EN,
  input  Load,
  output out_5,
  output [7:0] cur_val
);

  wire multiplexer_1_out, multiplexer_2_out, multiplexer_3_out, multiplexer_4_out, multiplexer_5_out,
       multiplexer_6_out, multiplexer_7_out, multiplexer_8_out, multiplexer_9_out, multiplexer_10_out,
       multiplexer_11_out, multiplexer_12_out, multiplexer_13_out, multiplexer_14_out, multiplexer_15_out,
       multiplexer_16_out;

  Multiplexer multiplexer_1 (.in0(cur_val[7]), .in1(1'b0), .out(multiplexer_1_out), .sel(EN));
  D_Flip_Flop d_ff_1 (.D(multiplexer_2_out), .clk(clk), .Q(cur_val[7]));  // open: Qn, preset, reset
  Multiplexer multiplexer_2 (.in0(multiplexer_1_out), .in1(inpt[7]), .out(multiplexer_2_out), .sel(Load));
  Multiplexer multiplexer_3 (.in0(cur_val[6]), .in1(cur_val[7]), .out(multiplexer_3_out), .sel(EN));
  D_Flip_Flop d_ff_2 (.D(multiplexer_4_out), .clk(clk), .Q(cur_val[6]));  // open: Qn, preset, reset
  Multiplexer multiplexer_4 (.in0(multiplexer_3_out), .in1(inpt[6]), .out(multiplexer_4_out), .sel(Load));
  Multiplexer multiplexer_5 (.in0(cur_val[5]), .in1(cur_val[6]), .out(multiplexer_5_out), .sel(EN));
  D_Flip_Flop d_ff_3 (.D(multiplexer_6_out), .clk(clk), .Q(cur_val[5]));  // open: Qn, preset, reset
  Multiplexer multiplexer_6 (.in0(multiplexer_5_out), .in1(inpt[5]), .out(multiplexer_6_out), .sel(Load));
  Multiplexer multiplexer_7 (.in0(cur_val[4]), .in1(cur_val[5]), .out(multiplexer_7_out), .sel(EN));
  D_Flip_Flop d_ff_4 (.D(multiplexer_8_out), .clk(clk), .Q(cur_val[4]));  // open: Qn, preset, reset
  Multiplexer multiplexer_8 (.in0(multiplexer_7_out), .in1(inpt[4]), .out(multiplexer_8_out), .sel(Load));
  Multiplexer multiplexer_9 (.in0(cur_val[3]), .in1(cur_val[4]), .out(multiplexer_9_out), .sel(EN));
  D_Flip_Flop d_ff_5 (.D(multiplexer_10_out), .clk(clk), .Q(cur_val[3]));  // open: Qn, preset, reset
  Multiplexer multiplexer_10 (.in0(multiplexer_9_out), .in1(inpt[3]), .out(multiplexer_10_out), .sel(Load));
  Multiplexer multiplexer_11 (.in0(cur_val[2]), .in1(cur_val[3]), .out(multiplexer_11_out), .sel(EN));
  D_Flip_Flop d_ff_6 (.D(multiplexer_12_out), .clk(clk), .Q(cur_val[2]));  // open: Qn, preset, reset
  Multiplexer multiplexer_12 (.in0(multiplexer_11_out), .in1(inpt[2]), .out(multiplexer_12_out), .sel(Load));
  Multiplexer multiplexer_13 (.in0(cur_val[1]), .in1(cur_val[2]), .out(multiplexer_13_out), .sel(EN));
  D_Flip_Flop d_ff_7 (.D(multiplexer_14_out), .clk(clk), .Q(cur_val[1]));  // open: Qn, preset, reset
  Multiplexer multiplexer_14 (.in0(multiplexer_13_out), .in1(inpt[1]), .out(multiplexer_14_out), .sel(Load));
  Multiplexer multiplexer_15 (.in0(cur_val[0]), .in1(cur_val[1]), .out(multiplexer_15_out), .sel(EN));
  D_Flip_Flop d_ff_8 (.D(multiplexer_16_out), .clk(clk), .Q(cur_val[0]));  // open: Qn, preset, reset
  Multiplexer multiplexer_16 (.in0(multiplexer_15_out), .in1(inpt[0]), .out(multiplexer_16_out), .sel(Load));

  assign out_5 = cur_val[0];
endmodule

module Rgstr (
  input  [13:0] inpt,
  input  Clk,
  input  Reset,
  input  EP,
  output [13:0] cur_value
);

  wire multiplexer_1_out, multiplexer_2_out, multiplexer_3_out, multiplexer_4_out, multiplexer_5_out,
       multiplexer_6_out, multiplexer_7_out, multiplexer_8_out, multiplexer_9_out, multiplexer_10_out,
       multiplexer_11_out, multiplexer_12_out, multiplexer_13_out, multiplexer_14_out;

  D_Flip_Flop d_ff_1 (.D(multiplexer_1_out), .clk(Clk), .Q(cur_value[13]), .reset(Reset));  // open: Qn, preset
  Multiplexer multiplexer_1 (.in0(cur_value[13]), .in1(inpt[13]), .out(multiplexer_1_out), .sel(EP));
  D_Flip_Flop d_ff_2 (.D(multiplexer_2_out), .clk(Clk), .Q(cur_value[12]), .reset(Reset));  // open: Qn, preset
  Multiplexer multiplexer_2 (.in0(cur_value[12]), .in1(inpt[12]), .out(multiplexer_2_out), .sel(EP));
  D_Flip_Flop d_ff_3 (.D(multiplexer_3_out), .clk(Clk), .Q(cur_value[11]), .reset(Reset));  // open: Qn, preset
  Multiplexer multiplexer_3 (.in0(cur_value[11]), .in1(inpt[11]), .out(multiplexer_3_out), .sel(EP));
  D_Flip_Flop d_ff_4 (.D(multiplexer_4_out), .clk(Clk), .Q(cur_value[10]), .reset(Reset));  // open: Qn, preset
  Multiplexer multiplexer_4 (.in0(cur_value[10]), .in1(inpt[10]), .out(multiplexer_4_out), .sel(EP));
  D_Flip_Flop d_ff_5 (.D(multiplexer_5_out), .clk(Clk), .Q(cur_value[9]), .reset(Reset));  // open: Qn, preset
  Multiplexer multiplexer_5 (.in0(cur_value[9]), .in1(inpt[9]), .out(multiplexer_5_out), .sel(EP));
  D_Flip_Flop d_ff_6 (.D(multiplexer_6_out), .clk(Clk), .Q(cur_value[8]), .reset(Reset));  // open: Qn, preset
  Multiplexer multiplexer_6 (.in0(cur_value[8]), .in1(inpt[8]), .out(multiplexer_6_out), .sel(EP));
  D_Flip_Flop d_ff_7 (.D(multiplexer_7_out), .clk(Clk), .Q(cur_value[7]), .reset(Reset));  // open: Qn, preset
  Multiplexer multiplexer_7 (.in0(cur_value[7]), .in1(inpt[7]), .out(multiplexer_7_out), .sel(EP));
  D_Flip_Flop d_ff_8 (.D(multiplexer_8_out), .clk(Clk), .Q(cur_value[6]), .reset(Reset));  // open: Qn, preset
  Multiplexer multiplexer_8 (.in0(cur_value[6]), .in1(inpt[6]), .out(multiplexer_8_out), .sel(EP));
  D_Flip_Flop d_ff_9 (.D(multiplexer_9_out), .clk(Clk), .Q(cur_value[5]), .reset(Reset));  // open: Qn, preset
  Multiplexer multiplexer_9 (.in0(cur_value[5]), .in1(inpt[5]), .out(multiplexer_9_out), .sel(EP));
  D_Flip_Flop d_ff_10 (.D(multiplexer_10_out), .clk(Clk), .Q(cur_value[4]), .reset(Reset));  // open: Qn, preset
  Multiplexer multiplexer_10 (.in0(cur_value[4]), .in1(inpt[4]), .out(multiplexer_10_out), .sel(EP));
  D_Flip_Flop d_ff_11 (.D(multiplexer_11_out), .clk(Clk), .Q(cur_value[3]), .reset(Reset));  // open: Qn, preset
  Multiplexer multiplexer_11 (.in0(cur_value[3]), .in1(inpt[3]), .out(multiplexer_11_out), .sel(EP));
  D_Flip_Flop d_ff_12 (.D(multiplexer_12_out), .clk(Clk), .Q(cur_value[2]), .reset(Reset));  // open: Qn, preset
  Multiplexer multiplexer_12 (.in0(cur_value[2]), .in1(inpt[2]), .out(multiplexer_12_out), .sel(EP));
  D_Flip_Flop d_ff_13 (.D(multiplexer_13_out), .clk(Clk), .Q(cur_value[1]), .reset(Reset));  // open: Qn, preset
  Multiplexer multiplexer_13 (.in0(cur_value[1]), .in1(inpt[1]), .out(multiplexer_13_out), .sel(EP));
  D_Flip_Flop d_ff_14 (.D(multiplexer_14_out), .clk(Clk), .Q(cur_value[0]), .reset(Reset));  // open: Qn, preset
  Multiplexer multiplexer_14 (.in0(cur_value[0]), .in1(inpt[0]), .out(multiplexer_14_out), .sel(EP));
endmodule

module twos_comp (
  input  [7:0] num_in,
  output [7:0] out_2
);

  wire or_2_out, or_3_out, or_4_out, or_5_out, or_6_out, or_7_out;

  // OR_Gate or_1 has open pins: in0=num_in[7], in1=or_2_out, out=open
  xor xor_1 (out_2[7], num_in[7], or_2_out);
  or or_2 (or_2_out, num_in[6], or_3_out);
  xor xor_2 (out_2[6], num_in[6], or_3_out);
  or or_3 (or_3_out, num_in[5], or_4_out);
  xor xor_3 (out_2[5], num_in[5], or_4_out);
  or or_4 (or_4_out, num_in[4], or_5_out);
  xor xor_4 (out_2[4], num_in[4], or_5_out);
  or or_5 (or_5_out, num_in[3], or_6_out);
  xor xor_5 (out_2[3], num_in[3], or_6_out);
  or or_6 (or_6_out, num_in[2], or_7_out);
  or or_7 (or_7_out, num_in[1], num_in[0]);
  xor xor_6 (out_2[2], num_in[2], or_7_out);
  xor xor_7 (out_2[1], num_in[1], num_in[0]);

  assign out_2[0] = num_in[0];
endmodule

module binary_to_bcd (
  input  [15:0] in_1,
  output [3:0] a,
  output [3:0] b,
  output [3:0] c,
  output [3:0] d,
  output [3:0] e
);

  wire double_dabble_unit_individual_1_out_5, double_dabble_unit_individual_1_out_6,
       double_dabble_unit_individual_1_out_7, double_dabble_unit_individual_1_out_8,
       double_dabble_unit_individual_2_out_5, double_dabble_unit_individual_2_out_6,
       double_dabble_unit_individual_2_out_7, double_dabble_unit_individual_2_out_8,
       double_dabble_unit_individual_3_out_5, double_dabble_unit_individual_3_out_6,
       double_dabble_unit_individual_3_out_7, double_dabble_unit_individual_3_out_8,
       double_dabble_unit_individual_4_out_5, double_dabble_unit_individual_4_out_6,
       double_dabble_unit_individual_4_out_7, double_dabble_unit_individual_4_out_8,
       double_dabble_unit_individual_5_out_5, double_dabble_unit_individual_5_out_6,
       double_dabble_unit_individual_5_out_7, double_dabble_unit_individual_5_out_8,
       double_dabble_unit_individual_6_out_5, double_dabble_unit_individual_6_out_6,
       double_dabble_unit_individual_6_out_7, double_dabble_unit_individual_6_out_8,
       double_dabble_unit_individual_7_out_5, double_dabble_unit_individual_7_out_6,
       double_dabble_unit_individual_7_out_7, double_dabble_unit_individual_7_out_8,
       double_dabble_unit_individual_8_out_5, double_dabble_unit_individual_8_out_6,
       double_dabble_unit_individual_8_out_7, double_dabble_unit_individual_8_out_8,
       double_dabble_unit_individual_9_out_5, double_dabble_unit_individual_9_out_6,
       double_dabble_unit_individual_9_out_7, double_dabble_unit_individual_9_out_8,
       double_dabble_unit_individual_10_out_5, double_dabble_unit_individual_10_out_6,
       double_dabble_unit_individual_10_out_7, double_dabble_unit_individual_10_out_8,
       double_dabble_unit_individual_11_out_5, double_dabble_unit_individual_11_out_6,
       double_dabble_unit_individual_11_out_7, double_dabble_unit_individual_11_out_8,
       double_dabble_unit_individual_12_out_5, double_dabble_unit_individual_12_out_6,
       double_dabble_unit_individual_12_out_7, double_dabble_unit_individual_12_out_8,
       double_dabble_unit_individual_13_out_5, double_dabble_unit_individual_13_out_6,
       double_dabble_unit_individual_13_out_7, double_dabble_unit_individual_13_out_8,
       double_dabble_unit_individual_14_out_5, double_dabble_unit_individual_14_out_6,
       double_dabble_unit_individual_14_out_7, double_dabble_unit_individual_14_out_8,
       double_dabble_unit_individual_15_out_5, double_dabble_unit_individual_15_out_6,
       double_dabble_unit_individual_15_out_7, double_dabble_unit_individual_15_out_8,
       double_dabble_unit_individual_16_out_5, double_dabble_unit_individual_16_out_6,
       double_dabble_unit_individual_16_out_7, double_dabble_unit_individual_16_out_8,
       double_dabble_unit_individual_17_out_5, double_dabble_unit_individual_17_out_6,
       double_dabble_unit_individual_17_out_7, double_dabble_unit_individual_17_out_8,
       double_dabble_unit_individual_18_out_5, double_dabble_unit_individual_18_out_6,
       double_dabble_unit_individual_18_out_7, double_dabble_unit_individual_18_out_8,
       double_dabble_unit_individual_19_out_5, double_dabble_unit_individual_19_out_6,
       double_dabble_unit_individual_19_out_7, double_dabble_unit_individual_19_out_8,
       double_dabble_unit_individual_20_out_5, double_dabble_unit_individual_20_out_6,
       double_dabble_unit_individual_20_out_7, double_dabble_unit_individual_20_out_8,
       double_dabble_unit_individual_21_out_5, double_dabble_unit_individual_21_out_6,
       double_dabble_unit_individual_21_out_7, double_dabble_unit_individual_21_out_8,
       double_dabble_unit_individual_22_out_5, double_dabble_unit_individual_22_out_6,
       double_dabble_unit_individual_22_out_7, double_dabble_unit_individual_22_out_8,
       double_dabble_unit_individual_23_out_5, double_dabble_unit_individual_23_out_6,
       double_dabble_unit_individual_23_out_7, double_dabble_unit_individual_23_out_8,
       double_dabble_unit_individual_24_out_5, double_dabble_unit_individual_24_out_6,
       double_dabble_unit_individual_24_out_7, double_dabble_unit_individual_24_out_8,
       double_dabble_unit_individual_25_out_5, double_dabble_unit_individual_25_out_6,
       double_dabble_unit_individual_25_out_7, double_dabble_unit_individual_25_out_8,
       double_dabble_unit_individual_26_out_5, double_dabble_unit_individual_26_out_6,
       double_dabble_unit_individual_26_out_7, double_dabble_unit_individual_26_out_8,
       double_dabble_unit_individual_27_out_5, double_dabble_unit_individual_27_out_6,
       double_dabble_unit_individual_27_out_7, double_dabble_unit_individual_27_out_8,
       double_dabble_unit_individual_28_out_5, double_dabble_unit_individual_28_out_6,
       double_dabble_unit_individual_28_out_7, double_dabble_unit_individual_28_out_8,
       double_dabble_unit_individual_29_out_5, double_dabble_unit_individual_29_out_6,
       double_dabble_unit_individual_29_out_7, double_dabble_unit_individual_29_out_8,
       double_dabble_unit_individual_30_out_5, double_dabble_unit_individual_30_out_6,
       double_dabble_unit_individual_30_out_7, double_dabble_unit_individual_30_out_8;

  double_dabble_unit_individual double_dabble_unit_individual_1 (
    .in_1(in_1[13]), .in_2(in_1[14]), .in_3(in_1[15]), .in_4(1'b0),
    .out_5(double_dabble_unit_individual_1_out_5), .out_6(double_dabble_unit_individual_1_out_6),
    .out_7(double_dabble_unit_individual_1_out_7), .out_8(double_dabble_unit_individual_1_out_8));
  double_dabble_unit_individual double_dabble_unit_individual_2 (
    .in_1(in_1[12]), .in_2(double_dabble_unit_individual_1_out_5),
    .in_3(double_dabble_unit_individual_1_out_6), .in_4(double_dabble_unit_individual_1_out_7),
    .out_5(double_dabble_unit_individual_2_out_5), .out_6(double_dabble_unit_individual_2_out_6),
    .out_7(double_dabble_unit_individual_2_out_7), .out_8(double_dabble_unit_individual_2_out_8));
  double_dabble_unit_individual double_dabble_unit_individual_3 (
    .in_1(in_1[11]), .in_2(double_dabble_unit_individual_2_out_5),
    .in_3(double_dabble_unit_individual_2_out_6), .in_4(double_dabble_unit_individual_2_out_7),
    .out_5(double_dabble_unit_individual_3_out_5), .out_6(double_dabble_unit_individual_3_out_6),
    .out_7(double_dabble_unit_individual_3_out_7), .out_8(double_dabble_unit_individual_3_out_8));
  double_dabble_unit_individual double_dabble_unit_individual_4 (
    .in_1(in_1[10]), .in_2(double_dabble_unit_individual_3_out_5),
    .in_3(double_dabble_unit_individual_3_out_6), .in_4(double_dabble_unit_individual_3_out_7),
    .out_5(double_dabble_unit_individual_4_out_5), .out_6(double_dabble_unit_individual_4_out_6),
    .out_7(double_dabble_unit_individual_4_out_7), .out_8(double_dabble_unit_individual_4_out_8));
  double_dabble_unit_individual double_dabble_unit_individual_5 (
    .in_1(double_dabble_unit_individual_3_out_8), .in_2(double_dabble_unit_individual_2_out_8),
    .in_3(double_dabble_unit_individual_1_out_8), .in_4(1'b0), .out_5(double_dabble_unit_individual_5_out_5),
    .out_6(double_dabble_unit_individual_5_out_6), .out_7(double_dabble_unit_individual_5_out_7),
    .out_8(double_dabble_unit_individual_5_out_8));
  double_dabble_unit_individual double_dabble_unit_individual_6 (
    .in_1(in_1[9]), .in_2(double_dabble_unit_individual_4_out_5),
    .in_3(double_dabble_unit_individual_4_out_6), .in_4(double_dabble_unit_individual_4_out_7),
    .out_5(double_dabble_unit_individual_6_out_5), .out_6(double_dabble_unit_individual_6_out_6),
    .out_7(double_dabble_unit_individual_6_out_7), .out_8(double_dabble_unit_individual_6_out_8));
  double_dabble_unit_individual double_dabble_unit_individual_7 (
    .in_1(double_dabble_unit_individual_4_out_8), .in_2(double_dabble_unit_individual_5_out_5),
    .in_3(double_dabble_unit_individual_5_out_6), .in_4(double_dabble_unit_individual_5_out_7),
    .out_5(double_dabble_unit_individual_7_out_5), .out_6(double_dabble_unit_individual_7_out_6),
    .out_7(double_dabble_unit_individual_7_out_7), .out_8(double_dabble_unit_individual_7_out_8));
  double_dabble_unit_individual double_dabble_unit_individual_8 (
    .in_1(in_1[8]), .in_2(double_dabble_unit_individual_6_out_5),
    .in_3(double_dabble_unit_individual_6_out_6), .in_4(double_dabble_unit_individual_6_out_7),
    .out_5(double_dabble_unit_individual_8_out_5), .out_6(double_dabble_unit_individual_8_out_6),
    .out_7(double_dabble_unit_individual_8_out_7), .out_8(double_dabble_unit_individual_8_out_8));
  double_dabble_unit_individual double_dabble_unit_individual_9 (
    .in_1(double_dabble_unit_individual_6_out_8), .in_2(double_dabble_unit_individual_7_out_5),
    .in_3(double_dabble_unit_individual_7_out_6), .in_4(double_dabble_unit_individual_7_out_7),
    .out_5(double_dabble_unit_individual_9_out_5), .out_6(double_dabble_unit_individual_9_out_6),
    .out_7(double_dabble_unit_individual_9_out_7), .out_8(double_dabble_unit_individual_9_out_8));
  double_dabble_unit_individual double_dabble_unit_individual_10 (
    .in_1(in_1[7]), .in_2(double_dabble_unit_individual_8_out_5),
    .in_3(double_dabble_unit_individual_8_out_6), .in_4(double_dabble_unit_individual_8_out_7),
    .out_5(double_dabble_unit_individual_10_out_5), .out_6(double_dabble_unit_individual_10_out_6),
    .out_7(double_dabble_unit_individual_10_out_7), .out_8(double_dabble_unit_individual_10_out_8));
  double_dabble_unit_individual double_dabble_unit_individual_11 (
    .in_1(double_dabble_unit_individual_8_out_8), .in_2(double_dabble_unit_individual_9_out_5),
    .in_3(double_dabble_unit_individual_9_out_6), .in_4(double_dabble_unit_individual_9_out_7),
    .out_5(double_dabble_unit_individual_11_out_5), .out_6(double_dabble_unit_individual_11_out_6),
    .out_7(double_dabble_unit_individual_11_out_7), .out_8(double_dabble_unit_individual_11_out_8));
  double_dabble_unit_individual double_dabble_unit_individual_12 (
    .in_1(double_dabble_unit_individual_9_out_8), .in_2(double_dabble_unit_individual_7_out_8),
    .in_3(double_dabble_unit_individual_5_out_8), .in_4(1'b0),
    .out_5(double_dabble_unit_individual_12_out_5), .out_6(double_dabble_unit_individual_12_out_6),
    .out_7(double_dabble_unit_individual_12_out_7), .out_8(double_dabble_unit_individual_12_out_8));
  double_dabble_unit_individual double_dabble_unit_individual_13 (
    .in_1(in_1[6]), .in_2(double_dabble_unit_individual_10_out_5),
    .in_3(double_dabble_unit_individual_10_out_6), .in_4(double_dabble_unit_individual_10_out_7),
    .out_5(double_dabble_unit_individual_13_out_5), .out_6(double_dabble_unit_individual_13_out_6),
    .out_7(double_dabble_unit_individual_13_out_7), .out_8(double_dabble_unit_individual_13_out_8));
  double_dabble_unit_individual double_dabble_unit_individual_14 (
    .in_1(double_dabble_unit_individual_10_out_8), .in_2(double_dabble_unit_individual_11_out_5),
    .in_3(double_dabble_unit_individual_11_out_6), .in_4(double_dabble_unit_individual_11_out_7),
    .out_5(double_dabble_unit_individual_14_out_5), .out_6(double_dabble_unit_individual_14_out_6),
    .out_7(double_dabble_unit_individual_14_out_7), .out_8(double_dabble_unit_individual_14_out_8));
  double_dabble_unit_individual double_dabble_unit_individual_15 (
    .in_1(double_dabble_unit_individual_11_out_8), .in_2(double_dabble_unit_individual_12_out_5),
    .in_3(double_dabble_unit_individual_12_out_6), .in_4(double_dabble_unit_individual_12_out_7),
    .out_5(double_dabble_unit_individual_15_out_5), .out_6(double_dabble_unit_individual_15_out_6),
    .out_7(double_dabble_unit_individual_15_out_7), .out_8(double_dabble_unit_individual_15_out_8));
  double_dabble_unit_individual double_dabble_unit_individual_16 (
    .in_1(in_1[5]), .in_2(double_dabble_unit_individual_13_out_5),
    .in_3(double_dabble_unit_individual_13_out_6), .in_4(double_dabble_unit_individual_13_out_7),
    .out_5(double_dabble_unit_individual_16_out_5), .out_6(double_dabble_unit_individual_16_out_6),
    .out_7(double_dabble_unit_individual_16_out_7), .out_8(double_dabble_unit_individual_16_out_8));
  double_dabble_unit_individual double_dabble_unit_individual_17 (
    .in_1(double_dabble_unit_individual_13_out_8), .in_2(double_dabble_unit_individual_14_out_5),
    .in_3(double_dabble_unit_individual_14_out_6), .in_4(double_dabble_unit_individual_14_out_7),
    .out_5(double_dabble_unit_individual_17_out_5), .out_6(double_dabble_unit_individual_17_out_6),
    .out_7(double_dabble_unit_individual_17_out_7), .out_8(double_dabble_unit_individual_17_out_8));
  double_dabble_unit_individual double_dabble_unit_individual_18 (
    .in_1(double_dabble_unit_individual_14_out_8), .in_2(double_dabble_unit_individual_15_out_5),
    .in_3(double_dabble_unit_individual_15_out_6), .in_4(double_dabble_unit_individual_15_out_7),
    .out_5(double_dabble_unit_individual_18_out_5), .out_6(double_dabble_unit_individual_18_out_6),
    .out_7(double_dabble_unit_individual_18_out_7), .out_8(double_dabble_unit_individual_18_out_8));
  double_dabble_unit_individual double_dabble_unit_individual_19 (
    .in_1(in_1[4]), .in_2(double_dabble_unit_individual_16_out_5),
    .in_3(double_dabble_unit_individual_16_out_6), .in_4(double_dabble_unit_individual_16_out_7),
    .out_5(double_dabble_unit_individual_19_out_5), .out_6(double_dabble_unit_individual_19_out_6),
    .out_7(double_dabble_unit_individual_19_out_7), .out_8(double_dabble_unit_individual_19_out_8));
  double_dabble_unit_individual double_dabble_unit_individual_20 (
    .in_1(double_dabble_unit_individual_16_out_8), .in_2(double_dabble_unit_individual_17_out_5),
    .in_3(double_dabble_unit_individual_17_out_6), .in_4(double_dabble_unit_individual_17_out_7),
    .out_5(double_dabble_unit_individual_20_out_5), .out_6(double_dabble_unit_individual_20_out_6),
    .out_7(double_dabble_unit_individual_20_out_7), .out_8(double_dabble_unit_individual_20_out_8));
  double_dabble_unit_individual double_dabble_unit_individual_21 (
    .in_1(double_dabble_unit_individual_17_out_8), .in_2(double_dabble_unit_individual_18_out_5),
    .in_3(double_dabble_unit_individual_18_out_6), .in_4(double_dabble_unit_individual_18_out_7),
    .out_5(double_dabble_unit_individual_21_out_5), .out_6(double_dabble_unit_individual_21_out_6),
    .out_7(double_dabble_unit_individual_21_out_7), .out_8(double_dabble_unit_individual_21_out_8));
  double_dabble_unit_individual double_dabble_unit_individual_22 (
    .in_1(double_dabble_unit_individual_18_out_8), .in_2(double_dabble_unit_individual_15_out_8),
    .in_3(double_dabble_unit_individual_12_out_8), .in_4(1'b0),
    .out_5(double_dabble_unit_individual_22_out_5), .out_6(double_dabble_unit_individual_22_out_6),
    .out_7(double_dabble_unit_individual_22_out_7), .out_8(double_dabble_unit_individual_22_out_8));
  double_dabble_unit_individual double_dabble_unit_individual_23 (
    .in_1(in_1[3]), .in_2(double_dabble_unit_individual_19_out_5),
    .in_3(double_dabble_unit_individual_19_out_6), .in_4(double_dabble_unit_individual_19_out_7),
    .out_5(double_dabble_unit_individual_23_out_5), .out_6(double_dabble_unit_individual_23_out_6),
    .out_7(double_dabble_unit_individual_23_out_7), .out_8(double_dabble_unit_individual_23_out_8));
  double_dabble_unit_individual double_dabble_unit_individual_24 (
    .in_1(double_dabble_unit_individual_19_out_8), .in_2(double_dabble_unit_individual_20_out_5),
    .in_3(double_dabble_unit_individual_20_out_6), .in_4(double_dabble_unit_individual_20_out_7),
    .out_5(double_dabble_unit_individual_24_out_5), .out_6(double_dabble_unit_individual_24_out_6),
    .out_7(double_dabble_unit_individual_24_out_7), .out_8(double_dabble_unit_individual_24_out_8));
  double_dabble_unit_individual double_dabble_unit_individual_25 (
    .in_1(double_dabble_unit_individual_20_out_8), .in_2(double_dabble_unit_individual_21_out_5),
    .in_3(double_dabble_unit_individual_21_out_6), .in_4(double_dabble_unit_individual_21_out_7),
    .out_5(double_dabble_unit_individual_25_out_5), .out_6(double_dabble_unit_individual_25_out_6),
    .out_7(double_dabble_unit_individual_25_out_7), .out_8(double_dabble_unit_individual_25_out_8));
  double_dabble_unit_individual double_dabble_unit_individual_26 (
    .in_1(double_dabble_unit_individual_21_out_8), .in_2(double_dabble_unit_individual_22_out_5),
    .in_3(double_dabble_unit_individual_22_out_6), .in_4(double_dabble_unit_individual_22_out_7),
    .out_5(double_dabble_unit_individual_26_out_5), .out_6(double_dabble_unit_individual_26_out_6),
    .out_7(double_dabble_unit_individual_26_out_7), .out_8(double_dabble_unit_individual_26_out_8));
  double_dabble_unit_individual double_dabble_unit_individual_27 (
    .in_1(in_1[2]), .in_2(double_dabble_unit_individual_23_out_5),
    .in_3(double_dabble_unit_individual_23_out_6), .in_4(double_dabble_unit_individual_23_out_7),
    .out_5(double_dabble_unit_individual_27_out_5), .out_6(double_dabble_unit_individual_27_out_6),
    .out_7(double_dabble_unit_individual_27_out_7), .out_8(double_dabble_unit_individual_27_out_8));
  double_dabble_unit_individual double_dabble_unit_individual_28 (
    .in_1(double_dabble_unit_individual_23_out_8), .in_2(double_dabble_unit_individual_24_out_5),
    .in_3(double_dabble_unit_individual_24_out_6), .in_4(double_dabble_unit_individual_24_out_7),
    .out_5(double_dabble_unit_individual_28_out_5), .out_6(double_dabble_unit_individual_28_out_6),
    .out_7(double_dabble_unit_individual_28_out_7), .out_8(double_dabble_unit_individual_28_out_8));
  double_dabble_unit_individual double_dabble_unit_individual_29 (
    .in_1(double_dabble_unit_individual_24_out_8), .in_2(double_dabble_unit_individual_25_out_5),
    .in_3(double_dabble_unit_individual_25_out_6), .in_4(double_dabble_unit_individual_25_out_7),
    .out_5(double_dabble_unit_individual_29_out_5), .out_6(double_dabble_unit_individual_29_out_6),
    .out_7(double_dabble_unit_individual_29_out_7), .out_8(double_dabble_unit_individual_29_out_8));
  double_dabble_unit_individual double_dabble_unit_individual_30 (
    .in_1(double_dabble_unit_individual_25_out_8), .in_2(double_dabble_unit_individual_26_out_5),
    .in_3(double_dabble_unit_individual_26_out_6), .in_4(double_dabble_unit_individual_26_out_7),
    .out_5(double_dabble_unit_individual_30_out_5), .out_6(double_dabble_unit_individual_30_out_6),
    .out_7(double_dabble_unit_individual_30_out_7), .out_8(double_dabble_unit_individual_30_out_8));
  double_dabble_unit_individual double_dabble_unit_individual_31 (
    .in_1(in_1[1]), .in_2(double_dabble_unit_individual_27_out_5),
    .in_3(double_dabble_unit_individual_27_out_6), .in_4(double_dabble_unit_individual_27_out_7),
    .out_5(a[1]), .out_6(a[2]), .out_7(a[3]), .out_8(b[0]));
  double_dabble_unit_individual double_dabble_unit_individual_32 (
    .in_1(double_dabble_unit_individual_27_out_8), .in_2(double_dabble_unit_individual_28_out_5),
    .in_3(double_dabble_unit_individual_28_out_6), .in_4(double_dabble_unit_individual_28_out_7),
    .out_5(b[1]), .out_6(b[2]), .out_7(b[3]), .out_8(c[0]));
  double_dabble_unit_individual double_dabble_unit_individual_33 (
    .in_1(double_dabble_unit_individual_28_out_8), .in_2(double_dabble_unit_individual_29_out_5),
    .in_3(double_dabble_unit_individual_29_out_6), .in_4(double_dabble_unit_individual_29_out_7),
    .out_5(c[1]), .out_6(c[2]), .out_7(c[3]), .out_8(d[0]));
  double_dabble_unit_individual double_dabble_unit_individual_34 (
    .in_1(double_dabble_unit_individual_29_out_8), .in_2(double_dabble_unit_individual_30_out_5),
    .in_3(double_dabble_unit_individual_30_out_6), .in_4(double_dabble_unit_individual_30_out_7),
    .out_5(d[1]), .out_6(d[2]), .out_7(d[3]), .out_8(e[0]));
  double_dabble_unit_individual double_dabble_unit_individual_35 (
    .in_1(double_dabble_unit_individual_30_out_8), .in_2(double_dabble_unit_individual_26_out_8),
    .in_3(double_dabble_unit_individual_22_out_8), .in_4(1'b0), .out_5(e[1]), .out_6(e[2]), .out_7(e[3]));  // open: out_8

  assign a[0] = in_1[0];
endmodule

module double_dabble_unit_individual (
  input  in_1,
  input  in_2,
  input  in_3,
  input  in_4,
  output out_5,
  output out_6,
  output out_7,
  output out_8
);

  wire comparator_1_gt;
  wire [3:0] adder_1_out;

  Adder #(.width(4)) adder_1 (.a({in_4, in_3, in_2, in_1}), .b(4'b0011), .out(adder_1_out), .cin(1'b0));  // open: cout
  Comparator #(.mode("unsigned"), .width(4)) comparator_1 (
    .a({in_4, in_3, in_2, in_1}), .b(4'b0100), .gt(comparator_1_gt));  // open: eq, lt
  Multiplexer #(.width(4)) multiplexer_1 (
    .in0({in_4, in_3, in_2, in_1}), .in1(adder_1_out), .out({out_8, out_7, out_6, out_5}),
    .sel(comparator_1_gt));
endmodule

module Display (
  input  in_1,
  input  [1:0] in_2,
  input  [13:0] in_3
);

  wire [3:0] binary_to_bcd_1_a, binary_to_bcd_1_b, binary_to_bcd_1_c, binary_to_bcd_1_d, binary_to_bcd_1_e;

  binary_to_bcd binary_to_bcd_1 (
    .in_1({2'b00, in_3}), .a(binary_to_bcd_1_a), .b(binary_to_bcd_1_b), .c(binary_to_bcd_1_c),
    .d(binary_to_bcd_1_d), .e(binary_to_bcd_1_e));
  _7_Segment_Display u_7_segment_display_1 (.g(in_1));  // open: f, a, b, e, d, c, dp
  _7_Segment_Display u_7_segment_display_2 ();  // open: g, f, a, b, e, d, c, dp
  _7_Segment_Display u_7_segment_display_3 ();  // open: g, f, a, b, e, d, c, dp
  // BCD_to_7_Segment_decoder bcd_to_7_segment_decoder_1: pin names not known
  // BCD_to_7_Segment_decoder bcd_to_7_segment_decoder_2: pin names not known
  Multiplexer #(.select(2), .width(4)) multiplexer_1 (
    .in0(binary_to_bcd_1_c), .in1(binary_to_bcd_1_d), .in2(binary_to_bcd_1_e), .sel(in_2));  // open: in3, out
  Multiplexer #(.select(2), .width(4)) multiplexer_2 (
    .in0(binary_to_bcd_1_b), .in1(binary_to_bcd_1_c), .in2(binary_to_bcd_1_d), .sel(in_2));  // open: in3, out
  _7_Segment_Display u_7_segment_display_4 ();  // open: g, f, a, b, e, d, c, dp
  // BCD_to_7_Segment_decoder bcd_to_7_segment_decoder_3: pin names not known
  Multiplexer #(.select(2), .width(4)) multiplexer_3 (
    .in0(binary_to_bcd_1_a), .in1(binary_to_bcd_1_b), .in2(binary_to_bcd_1_c), .sel(in_2));  // open: in3, out
endmodule
