// Logisim project logisim_circ.circ as structural Verilog: 9 circuits, main circuit main
module main (
  input  [15:0] in_1,
  input  reset
);

  wire and_1_out, bcd_to_7_segment_decoder_1_p1, bcd_to_7_segment_decoder_1_p2,
       bcd_to_7_segment_decoder_1_p3, bcd_to_7_segment_decoder_1_p6, bcd_to_7_segment_decoder_1_p7,
       bcd_to_7_segment_decoder_1_p8, bcd_to_7_segment_decoder_2_p1, bcd_to_7_segment_decoder_2_p2,
       bcd_to_7_segment_decoder_2_p3, bcd_to_7_segment_decoder_2_p4, bcd_to_7_segment_decoder_2_p6,
       bcd_to_7_segment_decoder_2_p7, bcd_to_7_segment_decoder_2_p8, bcd_to_7_segment_decoder_3_p1,
       bcd_to_7_segment_decoder_3_p2, bcd_to_7_segment_decoder_3_p3, bcd_to_7_segment_decoder_3_p4,
       bcd_to_7_segment_decoder_3_p6, bcd_to_7_segment_decoder_3_p7, bcd_to_7_segment_decoder_3_p8,
       bcd_to_7_segment_decoder_4_p1, bcd_to_7_segment_decoder_4_p2, bcd_to_7_segment_decoder_4_p3,
       bcd_to_7_segment_decoder_4_p4, bcd_to_7_segment_decoder_4_p6, bcd_to_7_segment_decoder_4_p7,
       bcd_to_7_segment_decoder_4_p8, bcd_to_7_segment_decoder_5_p1, bcd_to_7_segment_decoder_5_p2,
       bcd_to_7_segment_decoder_5_p3, bcd_to_7_segment_decoder_5_p4, bcd_to_7_segment_decoder_5_p6,
       bcd_to_7_segment_decoder_5_p7, bcd_to_7_segment_decoder_5_p8, bcd_to_7_segment_decoder_5_p9,
       clock_1_out, counter_1_carry, not_1_out, undriven;
  wire [3:0] bcd_to_7_segment_decoder_1_p5, bcd_to_7_segment_decoder_3_p5, bcd_to_7_segment_decoder_4_p5,
       counter_1_q, double_dabble_unit_1_num_out, multiplexer_1_out;
  wire [3:3] bcd_to_7_segment_decoder_1_p5_2;

  Multiplexer #(.select(4)) multiplexer_1 (
    .in0(in_1[15]), .in1(in_1[14]), .in2(in_1[13]), .in3(in_1[12]), .in4(in_1[11]), .in5(in_1[10]),
    .in6(in_1[9]), .in7(in_1[8]), .in8(in_1[7]), .in9(in_1[6]), .in10(in_1[5]), .in11(in_1[4]),
    .in12(in_1[3]), .in13(in_1[2]), .in14(in_1[1]), .in15(in_1[0]), .out(multiplexer_1_out[0]),
    .sel(counter_1_q));
  Clock clock_1 (.out(clock_1_out));
  Counter #(.max('hf), .width(4)) counter_1 (
    .count(1'b1), .Q(counter_1_q), .carry(counter_1_carry), .up(1'b1), .clk(and_1_out), .clr(reset));  // open: load, D
  not not_1 (not_1_out, counter_1_carry);
  // BCD_to_7_Segment_decoder bcd_to_7_segment_decoder_1: pin names not known; wires that end beside it: bcd_to_7_segment_decoder_1_p1, bcd_to_7_segment_decoder_1_p2, bcd_to_7_segment_decoder_1_p3, bcd_to_7_segment_decoder_1_p3, {bcd_to_7_segment_decoder_1_p5_2[3], bcd_to_7_segment_decoder_1_p5[3:1]}, bcd_to_7_segment_decoder_1_p6, bcd_to_7_segment_decoder_1_p7, bcd_to_7_segment_decoder_1_p8
  and and_1 (and_1_out, clock_1_out, not_1_out);
  _7_Segment_Display u_7_segment_display_1 (
    .g(bcd_to_7_segment_decoder_1_p1), .f(bcd_to_7_segment_decoder_1_p2), .a(bcd_to_7_segment_decoder_1_p6),
    .b(bcd_to_7_segment_decoder_1_p8), .e(undriven), .d(undriven), .c(bcd_to_7_segment_decoder_1_p7));  // open: dp
  _7_Segment_Display u_7_segment_display_2 (
    .g(bcd_to_7_segment_decoder_2_p1), .f(bcd_to_7_segment_decoder_2_p3), .a(bcd_to_7_segment_decoder_2_p6),
    .b(bcd_to_7_segment_decoder_2_p8), .e(bcd_to_7_segment_decoder_2_p2), .d(bcd_to_7_segment_decoder_2_p4),
    .c(bcd_to_7_segment_decoder_2_p7));  // open: dp
  // BCD_to_7_Segment_decoder bcd_to_7_segment_decoder_2: pin names not known; wires that end beside it: bcd_to_7_segment_decoder_2_p1, bcd_to_7_segment_decoder_2_p2, bcd_to_7_segment_decoder_2_p3, bcd_to_7_segment_decoder_2_p4, {bcd_to_7_segment_decoder_1_p5[0], bcd_to_7_segment_decoder_3_p5[3:1]}, bcd_to_7_segment_decoder_2_p6, bcd_to_7_segment_decoder_2_p7, bcd_to_7_segment_decoder_2_p8
  // BCD_to_7_Segment_decoder bcd_to_7_segment_decoder_3: pin names not known; wires that end beside it: bcd_to_7_segment_decoder_3_p1, bcd_to_7_segment_decoder_3_p2, bcd_to_7_segment_decoder_3_p3, bcd_to_7_segment_decoder_3_p4, {bcd_to_7_segment_decoder_3_p5[0], bcd_to_7_segment_decoder_4_p5[3:1]}, bcd_to_7_segment_decoder_3_p6, bcd_to_7_segment_decoder_3_p7, bcd_to_7_segment_decoder_3_p8
  double_dabble_unit double_dabble_unit_1 (
    .num_in(multiplexer_1_out), .clk(and_1_out), .rst(reset),
    .num_out({double_dabble_unit_1_num_out[0], multiplexer_1_out[3:1]}));
  _7_Segment_Display u_7_segment_display_3 (
    .g(bcd_to_7_segment_decoder_3_p1), .f(bcd_to_7_segment_decoder_3_p3), .a(bcd_to_7_segment_decoder_3_p6),
    .b(bcd_to_7_segment_decoder_3_p8), .e(bcd_to_7_segment_decoder_3_p2), .d(bcd_to_7_segment_decoder_3_p4),
    .c(bcd_to_7_segment_decoder_3_p7));  // open: dp
  // BCD_to_7_Segment_decoder bcd_to_7_segment_decoder_4: pin names not known; wires that end beside it: bcd_to_7_segment_decoder_4_p1, bcd_to_7_segment_decoder_4_p2, bcd_to_7_segment_decoder_4_p3, bcd_to_7_segment_decoder_4_p4, {bcd_to_7_segment_decoder_4_p5[0], double_dabble_unit_1_num_out[3:1]}, bcd_to_7_segment_decoder_4_p6, bcd_to_7_segment_decoder_4_p7, bcd_to_7_segment_decoder_4_p8
  _7_Segment_Display u_7_segment_display_4 (
    .g(bcd_to_7_segment_decoder_4_p1), .f(bcd_to_7_segment_decoder_4_p3), .a(bcd_to_7_segment_decoder_4_p6),
    .b(bcd_to_7_segment_decoder_4_p8), .e(bcd_to_7_segment_decoder_4_p2), .d(bcd_to_7_segment_decoder_4_p4),
    .c(bcd_to_7_segment_decoder_4_p7));  // open: dp
  _7_Segment_Display u_7_segment_display_5 (
    .g(bcd_to_7_segment_decoder_5_p1), .f(bcd_to_7_segment_decoder_5_p3), .a(bcd_to_7_segment_decoder_5_p6),
    .b(bcd_to_7_segment_decoder_5_p8), .e(bcd_to_7_segment_decoder_5_p2), .d(bcd_to_7_segment_decoder_5_p4),
    .c(bcd_to_7_segment_decoder_5_p7));  // open: dp
  // BCD_to_7_Segment_decoder bcd_to_7_segment_decoder_5: pin names not known; wires that end beside it: bcd_to_7_segment_decoder_5_p1, bcd_to_7_segment_decoder_5_p2, bcd_to_7_segment_decoder_5_p3, bcd_to_7_segment_decoder_5_p4, {double_dabble_unit_1_num_out[0], multiplexer_1_out[3:1]}, bcd_to_7_segment_decoder_5_p6, bcd_to_7_segment_decoder_5_p7, bcd_to_7_segment_decoder_5_p8, bcd_to_7_segment_decoder_5_p9, bcd_to_7_segment_decoder_5_p9
  double_dabble_unit double_dabble_unit_2 (
    .num_in(double_dabble_unit_1_num_out), .clk(and_1_out), .rst(reset),
    .num_out({bcd_to_7_segment_decoder_4_p5[0], double_dabble_unit_1_num_out[3:1]}));
  double_dabble_unit double_dabble_unit_3 (
    .num_in(bcd_to_7_segment_decoder_4_p5), .clk(and_1_out), .rst(reset),
    .num_out({bcd_to_7_segment_decoder_3_p5[0], bcd_to_7_segment_decoder_4_p5[3:1]}));
  double_dabble_unit double_dabble_unit_4 (
    .num_in(bcd_to_7_segment_decoder_3_p5), .clk(and_1_out), .rst(reset),
    .num_out({bcd_to_7_segment_decoder_1_p5[0], bcd_to_7_segment_decoder_3_p5[3:1]}));
  double_dabble_unit double_dabble_unit_5 (
    .num_in(bcd_to_7_segment_decoder_1_p5), .clk(and_1_out), .rst(reset),
    .num_out({bcd_to_7_segment_decoder_1_p5_2[3], bcd_to_7_segment_decoder_1_p5[3:1]}));
endmodule

module twos_comp (
  input  [7:0] num_in,
  output [7:0] out_2
);

  wire or_2_out, or_3_out, or_4_out, or_5_out, or_6_out, or_7_out;

  // OR_Gate or_1 has open pins: in0=num_in[7], in1=or_2_out, out=open
  xor xor_1 (out_2[7], num_in[7], or_2_out);
  or or_2 (or_2_out, num_in[6], or_3_out);
  xor xor_2 (out_2[6], num_in[6], or_3_out);
  or or_3 (or_3_out, num_in[5], or_4_out);
  xor xor_3 (out_2[5], num_in[5], or_4_out);
  or or_4 (or_4_out, num_in[4], or_5_out);
  xor xor_4 (out_2[4], num_in[4], or_5_out);
  or or_5 (or_5_out, num_in[3], or_6_out);
  xor xor_5 (out_2[3], num_in[3], or_6_out);
  or or_6 (or_6_out, num_in[2], or_7_out);
  or or_7 (or_7_out, num_in[1], num_in[0]);
  xor xor_6 (out_2[2], num_in[2], or_7_out);
  xor xor_7 (out_2[1], num_in[1], num_in[0]);

  assign out_2[0] = num_in[0];
endmodule

module FullAdder (
  input  X,
  input  Y,
  input  Cin,
  output S,
  output Cout
);

  wire and_1_out, and_2_out, and_3_out;

  xor xor_1 (S, X, Y, Cin);
  and and_1 (and_1_out, X, Y);
  and and_2 (and_2_out, Y, Cin);
  and and_3 (and_3_out, X, Cin);
  or or_1 (Cout, and_1_out, and_2_out, and_3_out);
endmodule

module FourBitRCA (
  input  [3:0] Y,
  input  [3:0] X,
  input  Cin
);

  wire fulladder_1_cout, fulladder_1_s, fulladder_2_cout, fulladder_2_s, fulladder_3_cout, fulladder_3_s,
       fulladder_4_cout, fulladder_4_s;

  FullAdder fulladder_1 (.X(X[0]), .Y(Y[0]), .Cin(Cin), .S(fulladder_1_s), .Cout(fulladder_1_cout));
  FullAdder fulladder_2 (.X(X[3]), .Y(Y[3]), .Cin(fulladder_4_cout), .S(fulladder_2_s), .Cout(fulladder_2_cout));
  FullAdder fulladder_3 (.X(X[1]), .Y(Y[1]), .Cin(fulladder_1_cout), .S(fulladder_3_s), .Cout(fulladder_3_cout));
  FullAdder fulladder_4 (.X(X[2]), .Y(Y[2]), .Cin(fulladder_3_cout), .S(fulladder_4_s), .Cout(fulladder_4_cout));
endmodule

module double_dabble_unit (
  input  [3:0] num_in,
  input  clk,
  input  rst,
  output [3:0] num_out
);

  wire comparator_1_gt;
  wire [3:0] adder_1_out, multiplexer_1_out;

  Adder #(.width(4)) adder_1 (.a(num_in), .b(4'b0011), .out(adder_1_out), .cin(1'b0));  // open: cout
  Comparator #(.width(4)) comparator_1 (.a(num_in), .b(4'b0100), .gt(comparator_1_gt));  // open: eq, lt
  Register #(.width(4)) register_1 (.D(multiplexer_1_out), .clk(clk), .Q(num_out), .clr(rst));  // open: en
  Multiplexer #(.width(4)) multiplexer_1 (
    .in0(num_in), .in1(adder_1_out), .out(multiplexer_1_out), .sel(comparator_1_gt));
endmodule

module serial_binary_to_bcd (
  input  [15:0] in_1,
  input  reset
);

  wire and_1_out, bcd_to_7_segment_decoder_1_p1, bcd_to_7_segment_decoder_1_p2,
       bcd_to_7_segment_decoder_1_p3, bcd_to_7_segment_decoder_1_p6, bcd_to_7_segment_decoder_1_p7,
       bcd_to_7_segment_decoder_1_p8, bcd_to_7_segment_decoder_2_p1, bcd_to_7_segment_decoder_2_p2,
       bcd_to_7_segment_decoder_2_p3, bcd_to_7_segment_decoder_2_p4, bcd_to_7_segment_decoder_2_p6,
       bcd_to_7_segment_decoder_2_p7, bcd_to_7_segment_decoder_2_p8, bcd_to_7_segment_decoder_3_p1,
       bcd_to_7_segment_decoder_3_p2, bcd_to_7_segment_decoder_3_p3, bcd_to_7_segment_decoder_3_p4,
       bcd_to_7_segment_decoder_3_p6, bcd_to_7_segment_decoder_3_p7, bcd_to_7_segment_decoder_3_p8,
       bcd_to_7_segment_decoder_4_p1, bcd_to_7_segment_decoder_4_p2, bcd_to_7_segment_decoder_4_p3,
       bcd_to_7_segment_decoder_4_p4, bcd_to_7_segment_decoder_4_p6, bcd_to_7_segment_decoder_4_p7,
       bcd_to_7_segment_decoder_4_p8, bcd_to_7_segment_decoder_5_p1, bcd_to_7_segment_decoder_5_p2,
       bcd_to_7_segment_decoder_5_p3, bcd_to_7_segment_decoder_5_p4, bcd_to_7_segment_decoder_5_p6,
       bcd_to_7_segment_decoder_5_p7, bcd_to_7_segment_decoder_5_p8, bcd_to_7_segment_decoder_5_p9,
       clock_1_out, counter_1_carry, not_1_out, undriven;
  wire [3:0] bcd_to_7_segment_decoder_1_p5, bcd_to_7_segment_decoder_3_p5, bcd_to_7_segment_decoder_4_p5,
       counter_1_q, double_dabble_unit_1_num_out, multiplexer_1_out;
  wire [3:3] bcd_to_7_segment_decoder_1_p5_2;

  Multiplexer #(.select(4)) multiplexer_1 (
    .in0(in_1[15]), .in1(in_1[14]), .in2(in_1[13]), .in3(in_1[12]), .in4(in_1[11]), .in5(in_1[10]),
    .in6(in_1[9]), .in7(in_1[8]), .in8(in_1[7]), .in9(in_1[6]), .in10(in_1[5]), .in11(in_1[4]),
    .in12(in_1[3]), .in13(in_1[2]), .in14(in_1[1]), .in15(in_1[0]), .out(multiplexer_1_out[0]),
    .sel(counter_1_q));
  Clock clock_1 (.out(clock_1_out));
  Counter #(.max('hf), .width(4)) counter_1 (
    .count(1'b1), .Q(counter_1_q), .carry(counter_1_carry), .up(1'b1), .clk(and_1_out), .clr(reset));  // open: load, D
  not not_1 (not_1_out, counter_1_carry);
  // BCD_to_7_Segment_decoder bcd_to_7_segment_decoder_1: pin names not known; wires that end beside it: bcd_to_7_segment_decoder_1_p1, bcd_to_7_segment_decoder_1_p2, bcd_to_7_segment_decoder_1_p3, bcd_to_7_segment_decoder_1_p3, {bcd_to_7_segment_decoder_1_p5_2[3], bcd_to_7_segment_decoder_1_p5[3:1]}, bcd_to_7_segment_decoder_1_p6, bcd_to_7_segment_decoder_1_p7, bcd_to_7_segment_decoder_1_p8
  and and_1 (and_1_out, clock_1_out, not_1_out);
  _7_Segment_Display u_7_segment_display_1 (
    .g(bcd_to_7_segment_decoder_1_p1), .f(bcd_to_7_segment_decoder_1_p2), .a(bcd_to_7_segment_decoder_1_p6),
    .b(bcd_to_7_segment_decoder_1_p8), .e(undriven), .d(undriven), .c(bcd_to_7_segment_decoder_1_p7));  // open: dp
  _7_Segment_Display u_7_segment_display_2 (
    .g(bcd_to_7_segment_decoder_2_p1), .f(bcd_to_7_segment_decoder_2_p3), .a(bcd_to_7_segment_decoder_2_p6),
    .b(bcd_to_7_segment_decoder_2_p8), .e(bcd_to_7_segment_decoder_2_p2), .d(bcd_to_7_segment_decoder_2_p4),
    .c(bcd_to_7_segment_decoder_2_p7));  // open: dp
  // BCD_to_7_Segment_decoder bcd_to_7_segment_decoder_2: pin names not known; wires that end beside it: bcd_to_7_segment_decoder_2_p1, bcd_to_7_segment_decoder_2_p2, bcd_to_7_segment_decoder_2_p3, bcd_to_7_segment_decoder_2_p4, {bcd_to_7_segment_decoder_1_p5[0], bcd_to_7_segment_decoder_3_p5[3:1]}, bcd_to_7_segment_decoder_2_p6, bcd_to_7_segment_decoder_2_p7, bcd_to_7_segment_decoder_2_p8
  // BCD_to_7_Segment_decoder bcd_to_7_segment_decoder_3: pin names not known; wires that end beside it: bcd_to_7_segment_decoder_3_p1, bcd_to_7_segment_decoder_3_p2, bcd_to_7_segment_decoder_3_p3, bcd_to_7_segment_decoder_3_p4, {bcd_to_7_segment_decoder_3_p5[0], bcd_to_7_segment_decoder_4_p5[3:1]}, bcd_to_7_segment_decoder_3_p6, bcd_to_7_segment_decoder_3_p7, bcd_to_7_segment_decoder_3_p8
  double_dabble_unit double_dabble_unit_1 (
    .num_in(multiplexer_1_out), .clk(and_1_out), .rst(reset),
    .num_out({double_dabble_unit_1_num_out[0], multiplexer_1_out[3:1]}));
  _7_Segment_Display u_7_segment_display_3 (
    .g(bcd_to_7_segment_decoder_3_p1), .f(bcd_to_7_segment_decoder_3_p3), .a(bcd_to_7_segment_decoder_3_p6),
    .b(bcd_to_7_segment_decoder_3_p8), .e(bcd_to_7_segment_decoder_3_p2), .d(bcd_to_7_segment_decoder_3_p4),
    .c(bcd_to_7_segment_decoder_3_p7));  // open: dp
  // BCD_to_7_Segment_decoder bcd_to_7_segment_decoder_4: pin names not known; wires that end beside it: bcd_to_7_segment_decoder_4_p1, bcd_to_7_segment_decoder_4_p2, bcd_to_7_segment_decoder_4_p3, bcd_to_7_segment_decoder_4_p4, {bcd_to_7_segment_decoder_4_p5[0], double_dabble_unit_1_num_out[3:1]}, bcd_to_7_segment_decoder_4_p6, bcd_to_7_segment_decoder_4_p7, bcd_to_7_segment_decoder_4_p8
  _7_Segment_Display u_7_segment_display_4 (
    .g(bcd_to_7_segment_decoder_4_p1), .f(bcd_to_7_segment_decoder_4_p3), .a(bcd_to_7_segment_decoder_4_p6),
    .b(bcd_to_7_segment_decoder_4_p8), .e(bcd_to_7_segment_decoder_4_p2), .d(bcd_to_7_segment_decoder_4_p4),
    .c(bcd_to_7_segment_decoder_4_p7));  // open: dp
  _7_Segment_Display u_7_segment_display_5 (
    .g(bcd_to_7_segment_decoder_5_p1), .f(bcd_to_7_segment_decoder_5_p3), .a(bcd_to_7_segment_decoder_5_p6),
    .b(bcd_to_7_segment_decoder_5_p8), .e(bcd_to_7_segment_decoder_5_p2), .d(bcd_to_7_segment_decoder_5_p4),
    .c(bcd_to_7_segment_decoder_5_p7));  // open: dp
  // BCD_to_7_Segment_decoder bcd_to_7_segment_decoder_5: pin names not known; wires that end beside it: bcd_to_7_segment_decoder_5_p1, bcd_to_7_segment_decoder_5_p2, bcd_to_7_segment_decoder_5_p3, bcd_to_7_segment_decoder_5_p4, {double_dabble_unit_1_num_out[0], multiplexer_1_out[3:1]}, bcd_to_7_segment_decoder_5_p6, bcd_to_7_segment_decoder_5_p7, bcd_to_7_segment_decoder_5_p8, bcd_to_7_segment_decoder_5_p9, bcd_to_7_segment_decoder_5_p9
  double_dabble_unit double_dabble_unit_2 (
    .num_in(double_dabble_unit_1_num_out), .clk(and_1_out), .rst(reset),
    .num_out({bcd_to_7_segment_decoder_4_p5[0], double_dabble_unit_1_num_out[3:1]}));
  double_dabble_unit double_dabble_unit_3 (
    .num_in(bcd_to_7_segment_decoder_4_p5), .clk(and_1_out), .rst(reset),
    .num_out({bcd_to_7_segment_decoder_3_p5[0], bcd_to_7_segment_decoder_4_p5[3:1]}));
  double_dabble_unit double_dabble_unit_4 (
    .num_in(bcd_to_7_segment_decoder_3_p5), .clk(and_1_out), .rst(reset),
    .num_out({bcd_to_7_segment_decoder_1_p5[0], bcd_to_7_segment_decoder_3_p5[3:1]}));
  double_dabble_unit double_dabble_unit_5 (
    .num_in(bcd_to_7_segment_decoder_1_p5), .clk(and_1_out), .rst(reset),
    .num_out({bcd_to_7_segment_decoder_1_p5_2[3], bcd_to_7_segment_decoder_1_p5[3:1]}));
endmodule

module binary_to_bcd (
  input  [15:0] in_1,
  output [3:0] a,
  output [3:0] b,
  output [3:0] c,
  output [3:0] d,
  output [3:0] e
);

  wire double_dabble_unit_individual_1_out_5, double_dabble_unit_individual_1_out_6,
       double_dabble_unit_individual_1_out_7, double_dabble_unit_individual_1_out_8,
       double_dabble_unit_individual_2_out_5, double_dabble_unit_individual_2_out_6,
       double_dabble_unit_individual_2_out_7, double_dabble_unit_individual_2_out_8,
       double_dabble_unit_individual_3_out_5, double_dabble_unit_individual_3_out_6,
       double_dabble_unit_individual_3_out_7, double_dabble_unit_individual_3_out_8,
       double_dabble_unit_individual_4_out_5, double_dabble_unit_individual_4_out_6,
       double_dabble_unit_individual_4_out_7, double_dabble_unit_individual_4_out_8,
       double_dabble_unit_individual_5_out_5, double_dabble_unit_individual_5_out_6,
       double_dabble_unit_individual_5_out_7, double_dabble_unit_individual_5_out_8,
       double_dabble_unit_individual_6_out_5, double_dabble_unit_individual_6_out_6,
       double_dabble_unit_individual_6_out_7, double_dabble_unit_individual_6_out_8,
       double_dabble_unit_individual_7_out_5, double_dabble_unit_individual_7_out_6,
       double_dabble_unit_individual_7_out_7, double_dabble_unit_individual_7_out_8,
       double_dabble_unit_individual_8_out_5, double_dabble_unit_individual_8_out_6,
       double_dabble_unit_individual_8_out_7, double_dabble_unit_individual_8_out_8,
       double_dabble_unit_individual_9_out_5, double_dabble_unit_individual_9_out_6,
       double_dabble_unit_individual_9_out_7, double_dabble_unit_individual_9_out_8,
       double_dabble_unit_individual_10_out_5, double_dabble_unit_individual_10_out_6,
       double_dabble_unit_individual_10_out_7, double_dabble_unit_individual_10_out_8,
       double_dabble_unit_individual_11_out_5, double_dabble_unit_individual_11_out_6,
       double_dabble_unit_individual_11_out_7, double_dabble_unit_individual_11_out_8,
       double_dabble_unit_individual_12_out_5, double_dabble_unit_individual_12_out_6,
       double_dabble_unit_individual_12_out_7, double_dabble_unit_individual_12_out_8,
       double_dabble_unit_individual_13_out_5, double_dabble_unit_individual_13_out_6,
       double_dabble_unit_individual_13_out_7, double_dabble_unit_individual_13_out_8,
       double_dabble_unit_individual_14_out_5, double_dabble_unit_individual_14_out_6,
       double_dabble_unit_individual_14_out_7, double_dabble_unit_individual_14_out_8,
       double_dabble_unit_individual_15_out_5, double_dabble_unit_individual_15_out_6,
       double_dabble_unit_individual_15_out_7, double_dabble_unit_individual_15_out_8,
       double_dabble_unit_individual_16_out_5, double_dabble_unit_individual_16_out_6,
       double_dabble_unit_individual_16_out_7, double_dabble_unit_individual_16_out_8,
       double_dabble_unit_individual_17_out_5, double_dabble_unit_individual_17_out_6,
       double_dabble_unit_individual_17_out_7, double_dabble_unit_individual_17_out_8,
       double_dabble_unit_individual_18_out_5, double_dabble_unit_individual_18_out_6,
       double_dabble_unit_individual_18_out_7, double_dabble_unit_individual_18_out_8,
       double_dabble_unit_individual_19_out_5, double_dabble_unit_individual_19_out_6,
       double_dabble_unit_individual_19_out_7, double_dabble_unit_individual_19_out_8,
       double_dabble_unit_individual_20_out_5, double_dabble_unit_individual_20_out_6,
       double_dabble_unit_individual_20_out_7, double_dabble_unit_individual_20_out_8,
       double_dabble_unit_individual_21_out_5, double_dabble_unit_individual_21_out_6,
       double_dabble_unit_individual_21_out_7, double_dabble_unit_individual_21_out_8,
       double_dabble_unit_individual_22_out_5, double_dabble_unit_individual_22_out_6,
       double_dabble_unit_individual_22_out_7, double_dabble_unit_individual_22_out_8,
       double_dabble_unit_individual_23_out_5, double_dabble_unit_individual_23_out_6,
       double_dabble_unit_individual_23_out_7, double_dabble_unit_individual_23_out_8,
       double_dabble_unit_individual_24_out_5, double_dabble_unit_individual_24_out_6,
       double_dabble_unit_individual_24_out_7, double_dabble_unit_individual_24_out_8,
       double_dabble_unit_individual_25_out_5, double_dabble_unit_individual_25_out_6,
       double_dabble_unit_individual_25_out_7, double_dabble_unit_individual_25_out_8,
       double_dabble_unit_individual_26_out_5, double_dabble_unit_individual_26_out_6,
       double_dabble_unit_individual_26_out_7, double_dabble_unit_individual_26_out_8,
       double_dabble_unit_individual_27_out_5, double_dabble_unit_individual_27_out_6,
       double_dabble_unit_individual_27_out_7, double_dabble_unit_individual_27_out_8,
       double_dabble_unit_individual_28_out_5, double_dabble_unit_individual_28_out_6,
       double_dabble_unit_individual_28_out_7, double_dabble_unit_individual_28_out_8,
       double_dabble_unit_individual_29_out_5, double_dabble_unit_individual_29_out_6,
       double_dabble_unit_individual_29_out_7, double_dabble_unit_individual_29_out_8,
       double_dabble_unit_individual_30_out_5, double_dabble_unit_individual_30_out_6,
       double_dabble_unit_individual_30_out_7, double_dabble_unit_individual_30_out_8;

  double_dabble_unit_individual double_dabble_unit_individual_1 (
    .in_1(in_1[13]), .in_2(in_1[14]), .in_3(in_1[15]), .in_4(1'b0),
    .out_5(double_dabble_unit_individual_1_out_5), .out_6(double_dabble_unit_individual_1_out_6),
    .out_7(double_dabble_unit_individual_1_out_7), .out_8(double_dabble_unit_individual_1_out_8));
  double_dabble_unit_individual double_dabble_unit_individual_2 (
    .in_1(in_1[12]), .in_2(double_dabble_unit_individual_1_out_5),
    .in_3(double_dabble_unit_individual_1_out_6), .in_4(double_dabble_unit_individual_1_out_7),
    .out_5(double_dabble_unit_individual_2_out_5), .out_6(double_dabble_unit_individual_2_out_6),
    .out_7(double_dabble_unit_individual_2_out_7), .out_8(double_dabble_unit_individual_2_out_8));
  double_dabble_unit_individual double_dabble_unit_individual_3 (
    .in_1(in_1[11]), .in_2(double_dabble_unit_individual_2_out_5),
    .in_3(double_dabble_unit_individual_2_out_6), .in_4(double_dabble_unit_individual_2_out_7),
    .out_5(double_dabble_unit_individual_3_out_5), .out_6(double_dabble_unit_individual_3_out_6),
    .out_7(double_dabble_unit_individual_3_out_7), .out_8(double_dabble_unit_individual_3_out_8));
  double_dabble_unit_individual double_dabble_unit_individual_4 (
    .in_1(in_1[10]), .in_2(double_dabble_unit_individual_3_out_5),
    .in_3(double_dabble_unit_individual_3_out_6), .in_4(double_dabble_unit_individual_3_out_7),
    .out_5(double_dabble_unit_individual_4_out_5), .out_6(double_dabble_unit_individual_4_out_6),
    .out_7(double_dabble_unit_individual_4_out_7), .out_8(double_dabble_unit_individual_4_out_8));
  double_dabble_unit_individual double_dabble_unit_individual_5 (
    .in_1(double_dabble_unit_individual_3_out_8), .in_2(double_dabble_unit_individual_2_out_8),
    .in_3(double_dabble_unit_individual_1_out_8), .in_4(1'b0), .out_5(double_dabble_unit_individual_5_out_5),
    .out_6(double_dabble_unit_individual_5_out_6), .out_7(double_dabble_unit_individual_5_out_7),
    .out_8(double_dabble_unit_individual_5_out_8));
  double_dabble_unit_individual double_dabble_unit_individual_6 (
    .in_1(in_1[9]), .in_2(double_dabble_unit_individual_4_out_5),
    .in_3(double_dabble_unit_individual_4_out_6), .in_4(double_dabble_unit_individual_4_out_7),
    .out_5(double_dabble_unit_individual_6_out_5), .out_6(double_dabble_unit_individual_6_out_6),
    .out_7(double_dabble_unit_individual_6_out_7), .out_8(double_dabble_unit_individual_6_out_8));
  double_dabble_unit_individual double_dabble_unit_individual_7 (
    .in_1(double_dabble_unit_individual_4_out_8), .in_2(double_dabble_unit_individual_5_out_5),
    .in_3(double_dabble_unit_individual_5_out_6), .in_4(double_dabble_unit_individual_5_out_7),
    .out_5(double_dabble_unit_individual_7_out_5), .out_6(double_dabble_unit_individual_7_out_6),
    .out_7(double_dabble_unit_individual_7_out_7), .out_8(double_dabble_unit_individual_7_out_8));
  double_dabble_unit_individual double_dabble_unit_individual_8 (
    .in_1(in_1[8]), .in_2(double_dabble_unit_individual_6_out_5),
    .in_3(double_dabble_unit_individual_6_out_6), .in_4(double_dabble_unit_individual_6_out_7),
    .out_5(double_dabble_unit_individual_8_out_5), .out_6(double_dabble_unit_individual_8_out_6),
    .out_7(double_dabble_unit_individual_8_out_7), .out_8(double_dabble_unit_individual_8_out_8));
  double_dabble_unit_individual double_dabble_unit_individual_9 (
    .in_1(double_dabble_unit_individual_6_out_8), .in_2(double_dabble_unit_individual_7_out_5),
    .in_3(double_dabble_unit_individual_7_out_6), .in_4(double_dabble_unit_individual_7_out_7),
    .out_5(double_dabble_unit_individual_9_out_5), .out_6(double_dabble_unit_individual_9_out_6),
    .out_7(double_dabble_unit_individual_9_out_7), .out_8(double_dabble_unit_individual_9_out_8));
  double_dabble_unit_individual double_dabble_unit_individual_10 (
    .in_1(in_1[7]), .in_2(double_dabble_unit_individual_8_out_5),
    .in_3(double_dabble_unit_individual_8_out_6), .in_4(double_dabble_unit_individual_8_out_7),
    .out_5(double_dabble_unit_individual_10_out_5), .out_6(double_dabble_unit_individual_10_out_6),
    .out_7(double_dabble_unit_individual_10_out_7), .out_8(double_dabble_unit_individual_10_out_8));
  double_dabble_unit_individual double_dabble_unit_individual_11 (
    .in_1(double_dabble_unit_individual_8_out_8), .in_2(double_dabble_unit_individual_9_out_5),
    .in_3(double_dabble_unit_individual_9_out_6), .in_4(double_dabble_unit_individual_9_out_7),
    .out_5(double_dabble_unit_individual_11_out_5), .out_6(double_dabble_unit_individual_11_out_6),
    .out_7(double_dabble_unit_individual_11_out_7), .out_8(double_dabble_unit_individual_11_out_8));
  double_dabble_unit_individual double_dabble_unit_individual_12 (
    .in_1(double_dabble_unit_individual_9_out_8), .in_2(double_dabble_unit_individual_7_out_8),
    .in_3(double_dabble_unit_individual_5_out_8), .in_4(1'b0),
    .out_5(double_dabble_unit_individual_12_out_5), .out_6(double_dabble_unit_individual_12_out_6),
    .out_7(double_dabble_unit_individual_12_out_7), .out_8(double_dabble_unit_individual_12_out_8));
  double_dabble_unit_individual double_dabble_unit_individual_13 (
    .in_1(in_1[6]), .in_2(double_dabble_unit_individual_10_out_5),
    .in_3(double_dabble_unit_individual_10_out_6), .in_4(double_dabble_unit_individual_10_out_7),
    .out_5(double_dabble_unit_individual_13_out_5), .out_6(double_dabble_unit_individual_13_out_6),
    .out_7(double_dabble_unit_individual_13_out_7), .out_8(double_dabble_unit_individual_13_out_8));
  double_dabble_unit_individual double_dabble_unit_individual_14 (
    .in_1(double_dabble_unit_individual_10_out_8), .in_2(double_dabble_unit_individual_11_out_5),
    .in_3(double_dabble_unit_individual_11_out_6), .in_4(double_dabble_unit_individual_11_out_7),
    .out_5(double_dabble_unit_individual_14_out_5), .out_6(double_dabble_unit_individual_14_out_6),
    .out_7(double_dabble_unit_individual_14_out_7), .out_8(double_dabble_unit_individual_14_out_8));
  double_dabble_unit_individual double_dabble_unit_individual_15 (
    .in_1(double_dabble_unit_individual_11_out_8), .in_2(double_dabble_unit_individual_12_out_5),
    .in_3(double_dabble_unit_individual_12_out_6), .in_4(double_dabble_unit_individual_12_out_7),
    .out_5(double_dabble_unit_individual_15_out_5), .out_6(double_dabble_unit_individual_15_out_6),
    .out_7(double_dabble_unit_individual_15_out_7), .out_8(double_dabble_unit_individual_15_out_8));
  double_dabble_unit_individual double_dabble_unit_individual_16 (
    .in_1(in_1[5]), .in_2(double_dabble_unit_individual_13_out_5),
    .in_3(double_dabble_unit_individual_13_out_6), .in_4(double_dabble_unit_individual_13_out_7),
    .out_5(double_dabble_unit_individual_16_out_5), .out_6(double_dabble_unit_individual_16_out_6),
    .out_7(double_dabble_unit_individual_16_out_7), .out_8(double_dabble_unit_individual_16_out_8));
  double_dabble_unit_individual double_dabble_unit_individual_17 (
    .in_1(double_dabble_unit_individual_13_out_8), .in_2(double_dabble_unit_individual_14_out_5),
    .in_3(double_dabble_unit_individual_14_out_6), .in_4(double_dabble_unit_individual_14_out_7),
    .out_5(double_dabble_unit_individual_17_out_5), .out_6(double_dabble_unit_individual_17_out_6),
    .out_7(double_dabble_unit_individual_17_out_7), .out_8(double_dabble_unit_individual_17_out_8));
  double_dabble_unit_individual double_dabble_unit_individual_18 (
    .in_1(double_dabble_unit_individual_14_out_8), .in_2(double_dabble_unit_individual_15_out_5),
    .in_3(double_dabble_unit_individual_15_out_6), .in_4(double_dabble_unit_individual_15_out_7),
    .out_5(double_dabble_unit_individual_18_out_5), .out_6(double_dabble_unit_individual_18_out_6),
    .out_7(double_dabble_unit_individual_18_out_7), .out_8(double_dabble_unit_individual_18_out_8));
  double_dabble_unit_individual double_dabble_unit_individual_19 (
    .in_1(in_1[4]), .in_2(double_dabble_unit_individual_16_out_5),
    .in_3(double_dabble_unit_individual_16_out_6), .in_4(double_dabble_unit_individual_16_out_7),
    .out_5(double_dabble_unit_individual_19_out_5), .out_6(double_dabble_unit_individual_19_out_6),
    .out_7(double_dabble_unit_individual_19_out_7), .out_8(double_dabble_unit_individual_19_out_8));
  double_dabble_unit_individual double_dabble_unit_individual_20 (
    .in_1(double_dabble_unit_individual_16_out_8), .in_2(double_dabble_unit_individual_17_out_5),
    .in_3(double_dabble_unit_individual_17_out_6), .in_4(double_dabble_unit_individual_17_out_7),
    .out_5(double_dabble_unit_individual_20_out_5), .out_6(double_dabble_unit_individual_20_out_6),
    .out_7(double_dabble_unit_individual_20_out_7), .out_8(double_dabble_unit_individual_20_out_8));
  double_dabble_unit_individual double_dabble_unit_individual_21 (
    .in_1(double_dabble_unit_individual_17_out_8), .in_2(double_dabble_unit_individual_18_out_5),
    .in_3(double_dabble_unit_individual_18_out_6), .in_4(double_dabble_unit_individual_18_out_7),
    .out_5(double_dabble_unit_individual_21_out_5), .out_6(double_dabble_unit_individual_21_out_6),
    .out_7(double_dabble_unit_individual_21_out_7), .out_8(double_dabble_unit_individual_21_out_8));
  double_dabble_unit_individual double_dabble_unit_individual_22 (
    .in_1(double_dabble_unit_individual_18_out_8), .in_2(double_dabble_unit_individual_15_out_8),
    .in_3(double_dabble_unit_individual_12_out_8), .in_4(1'b0),
    .out_5(double_dabble_unit_individual_22_out_5), .out_6(double_dabble_unit_individual_22_out_6),
    .out_7(double_dabble_unit_individual_22_out_7), .out_8(double_dabble_unit_individual_22_out_8));
  double_dabble_unit_individual double_dabble_unit_individual_23 (
    .in_1(in_1[3]), .in_2(double_dabble_unit_individual_19_out_5),
    .in_3(double_dabble_unit_individual_19_out_6), .in_4(double_dabble_unit_individual_19_out_7),
    .out_5(double_dabble_unit_individual_23_out_5), .out_6(double_dabble_unit_individual_23_out_6),
    .out_7(double_dabble_unit_individual_23_out_7), .out_8(double_dabble_unit_individual_23_out_8));
  double_dabble_unit_individual double_dabble_unit_individual_24 (
    .in_1(double_dabble_unit_individual_19_out_8), .in_2(double_dabble_unit_individual_20_out_5),
    .in_3(double_dabble_unit_individual_20_out_6), .in_4(double_dabble_unit_individual_20_out_7),
    .out_5(double_dabble_unit_individual_24_out_5), .out_6(double_dabble_unit_individual_24_out_6),
    .out_7(double_dabble_unit_individual_24_out_7), .out_8(double_dabble_unit_individual_24_out_8));
  double_dabble_unit_individual double_dabble_unit_individual_25 (
    .in_1(double_dabble_unit_individual_20_out_8), .in_2(double_dabble_unit_individual_21_out_5),
    .in_3(double_dabble_unit_individual_21_out_6), .in_4(double_dabble_unit_individual_21_out_7),
    .out_5(double_dabble_unit_individual_25_out_5), .out_6(double_dabble_unit_individual_25_out_6),
    .out_7(double_dabble_unit_individual_25_out_7), .out_8(double_dabble_unit_individual_25_out_8));
  double_dabble_unit_individual double_dabble_unit_individual_26 (
    .in_1(double_dabble_unit_individual_21_out_8), .in_2(double_dabble_unit_individual_22_out_5),
    .in_3(double_dabble_unit_individual_22_out_6), .in_4(double_dabble_unit_individual_22_out_7),
    .out_5(double_dabble_unit_individual_26_out_5), .out_6(double_dabble_unit_individual_26_out_6),
    .out_7(double_dabble_unit_individual_26_out_7), .out_8(double_dabble_unit_individual_26_out_8));
  double_dabble_unit_individual double_dabble_unit_individual_27 (
    .in_1(in_1[2]), .in_2(double_dabble_unit_individual_23_out_5),
    .in_3(double_dabble_unit_individual_23_out_6), .in_4(double_dabble_unit_individual_23_out_7),
    .out_5(double_dabble_unit_individual_27_out_5), .out_6(double_dabble_unit_individual_27_out_6),
    .out_7(double_dabble_unit_individual_27_out_7), .out_8(double_dabble_unit_individual_27_out_8));
  double_dabble_unit_individual double_dabble_unit_individual_28 (
    .in_1(double_dabble_unit_individual_23_out_8), .in_2(double_dabble_unit_individual_24_out_5),
    .in_3(double_dabble_unit_individual_24_out_6), .in_4(double_dabble_unit_individual_24_out_7),
    .out_5(double_dabble_unit_individual_28_out_5), .out_6(double_dabble_unit_individual_28_out_6),
    .out_7(double_dabble_unit_individual_28_out_7), .out_8(double_dabble_unit_individual_28_out_8));
  double_dabble_unit_individual double_dabble_unit_individual_29 (
    .in_1(double_dabble_unit_individual_24_out_8), .in_2(double_dabble_unit_individual_25_out_5),
    .in_3(double_dabble_unit_individual_25_out_6), .in_4(double_dabble_unit_individual_25_out_7),
    .out_5(double_dabble_unit_individual_29_out_5), .out_6(double_dabble_unit_individual_29_out_6),
    .out_7(double_dabble_unit_individual_29_out_7), .out_8(double_dabble_unit_individual_29_out_8));
  double_dabble_unit_individual double_dabble_unit_individual_30 (
    .in_1(double_dabble_unit_individual_25_out_8), .in_2(double_dabble_unit_individual_26_out_5),
    .in_3(double_dabble_unit_individual_26_out_6), .in_4(double_dabble_unit_individual_26_out_7),
    .out_5(double_dabble_unit_individual_30_out_5), .out_6(double_dabble_unit_individual_30_out_6),
    .out_7(double_dabble_unit_individual_30_out_7), .out_8(double_dabble_unit_individual_30_out_8));
  double_dabble_unit_individual double_dabble_unit_individual_31 (
    .in_1(in_1[1]), .in_2(double_dabble_unit_individual_27_out_5),
    .in_3(double_dabble_unit_individual_27_out_6), .in_4(double_dabble_unit_individual_27_out_7),
    .out_5(a[1]), .out_6(a[2]), .out_7(a[3]), .out_8(b[0]));
  double_dabble_unit_individual double_dabble_unit_individual_32 (
    .in_1(double_dabble_unit_individual_27_out_8), .in_2(double_dabble_unit_individual_28_out_5),
    .in_3(double_dabble_unit_individual_28_out_6), .in_4(double_dabble_unit_individual_28_out_7),
    .out_5(b[1]), .out_6(b[2]), .out_7(b[3]), .out_8(c[0]));
  double_dabble_unit_individual double_dabble_unit_individual_33 (
    .in_1(double_dabble_unit_individual_28_out_8), .in_2(double_dabble_unit_individual_29_out_5),
    .in_3(double_dabble_unit_individual_29_out_6), .in_4(double_dabble_unit_individual_29_out_7),
    .out_5(c[1]), .out_6(c[2]), .out_7(c[3]), .out_8(d[0]));
  double_dabble_unit_individual double_dabble_unit_individual_34 (
    .in_1(double_dabble_unit_individual_29_out_8), .in_2(double_dabble_unit_individual_30_out_5),
    .in_3(double_dabble_unit_individual_30_out_6), .in_4(double_dabble_unit_individual_30_out_7),
    .out_5(d[1]), .out_6(d[2]), .out_7(d[3]), .out_8(e[0]));
  double_dabble_unit_individual double_dabble_unit_individual_35 (
    .in_1(double_dabble_unit_individual_30_out_8), .in_2(double_dabble_unit_individual_26_out_8),
    .in_3(double_dabble_unit_individual_22_out_8), .in_4(1'b0), .out_5(e[1]), .out_6(e[2]), .out_7(e[3]));  // open: out_8

  assign a[0] = in_1[0];
endmodule

module double_dabble_unit_individual (
  input  in_1,
  input  in_2,
  input  in_3,
  input  in_4,
  output out_5,
  output out_6,
  output out_7,
  output out_8
);

  wire comparator_1_gt;
  wire [3:0] adder_1_out;

  Adder #(.width(4)) adder_1 (.a({in_4, in_3, in_2, in_1}), .b(4'b0011), .out(adder_1_out), .cin(1'b0));  // open: cout
  Comparator #(.mode("unsigned"), .width(4)) comparator_1 (
    .a({in_4, in_3, in_2, in_1}), .b(4'b0100), .gt(comparator_1_gt));  // open: eq, lt
  Multiplexer #(.width(4)) multiplexer_1 (
    .in0({in_4, in_3, in_2, in_1}), .in1(adder_1_out), .out({out_8, out_7, out_6, out_5}),
    .sel(comparator_1_gt));
endmodule

module Display (
  input  in_1,
  input  [1:0] in_2,
  input  [13:0] in_3
);

  wire [3:0] binary_to_bcd_1_a, binary_to_bcd_1_b, binary_to_bcd_1_c, binary_to_bcd_1_d, binary_to_bcd_1_e;

  binary_to_bcd binary_to_bcd_1 (
    .in_1({2'b00, in_3}), .a(binary_to_bcd_1_a), .b(binary_to_bcd_1_b), .c(binary_to_bcd_1_c),
    .d(binary_to_bcd_1_d), .e(binary_to_bcd_1_e));
  _7_Segment_Display u_7_segment_display_1 (.g(in_1));  // open: f, a, b, e, d, c, dp
  _7_Segment_Display u_7_segment_display_2 ();  // open: g, f, a, b, e, d, c, dp
  _7_Segment_Display u_7_segment_display_3 ();  // open: g, f, a, b, e, d, c, dp
  // BCD_to_7_Segment_decoder bcd_to_7_segment_decoder_1: pin names not known
  // BCD_to_7_Segment_decoder bcd_to_7_segment_decoder_2: pin names not known
  Multiplexer #(.select(2), .width(4)) multiplexer_1 (
    .in0(binary_to_bcd_1_c), .in1(binary_to_bcd_1_d), .in2(binary_to_bcd_1_e), .sel(in_2));  // open: in3, out
  Multiplexer #(.select(2), .width(4)) multiplexer_2 (
    .in0(binary_to_bcd_1_b), .in1(binary_to_bcd_1_c), .in2(binary_to_bcd_1_d), .sel(in_2));  // open: in3, out
  _7_Segment_Display u_7_segment_display_4 ();  // open: g, f, a, b, e, d, c, dp
  // BCD_to_7_Segment_decoder bcd_to_7_segment_decoder_3: pin names not known
  Multiplexer #(.select(2), .width(4)) multiplexer_3 (
    .in0(binary_to_bcd_1_a), .in1(binary_to_bcd_1_b), .in2(binary_to_bcd_1_c), .sel(in_2));  // open: in3, out
endmodule
